// Logisim project RV32IM.circ as structural Verilog: 11 circuits, main circuit main
module main (
);

  wire clock_1_out, rv32_control_unit_1_a_sel, rv32_control_unit_1_b_sel, rv32_control_unit_1_mem_r,
       rv32_control_unit_1_mem_w, rv32_control_unit_1_pc_sel, rv32_control_unit_1_reg_w;
  wire [1:0] rv32_control_unit_1_wb_sel;
  wire [2:0] rv32_control_unit_1_imm_sel, RV32_Instr_Mem_data_3;
  wire [3:0] rv32_control_unit_1_alu_op;
  wire [4:0] rv32_instr_split_1_r1, rv32_instr_split_1_r2, rv32_instr_split_1_rd;
  wire [6:0] RV32_Instr_Mem_data;
  wire [31:0] multiplexer_1_out, multiplexer_2_out, multiplexer_3_out, multiplexer_4_out, PC_pc_out,
       regfile_1_a_data, regfile_1_b_data, rv32_alu_1_alu_out, RV32_Data_Mem_dout, rv32_immgen_1_imm_out;
  wire [31:7] RV32_Instr_Mem_data_2;

  Multiplexer #(.width(32)) multiplexer_1 (
    .in0(PC_pc_out), .in1(rv32_alu_1_alu_out), .out(multiplexer_1_out), .sel(rv32_control_unit_1_pc_sel));
  Clock clock_1 (.out(clock_1_out));
  ROM #(.addrWidth(12), .dataWidth(32)) RV32_Instr_Mem (
    .addr(PC_pc_out[13:2]),
    .data({RV32_Instr_Mem_data_2[31:15], RV32_Instr_Mem_data_3, RV32_Instr_Mem_data_2[11:7], RV32_Instr_Mem_data}));
  rv32_pc PC (
    .Branch_Address(multiplexer_1_out), .Branch(rv32_control_unit_1_pc_sel), .Clock(clock_1_out),
    .PC_Out(PC_pc_out));  // open: ResetPC
  RV32_instr_split rv32_instr_split_1 (
    .Instr32({RV32_Instr_Mem_data_2[31:15], RV32_Instr_Mem_data_3, RV32_Instr_Mem_data_2[11:7], RV32_Instr_Mem_data}),
    .rd(rv32_instr_split_1_rd), .r2(rv32_instr_split_1_r2), .r1(rv32_instr_split_1_r1));  // open: opcode, funct3, funct7, to_Imm
  RV32_ImmGen rv32_immgen_1 (
    .Instr({RV32_Instr_Mem_data_2[31:15], RV32_Instr_Mem_data_3, RV32_Instr_Mem_data_2[11:7], RV32_Instr_Mem_data}),
    .Imm_Sel(rv32_control_unit_1_imm_sel), .Imm_Out(rv32_immgen_1_imm_out));
  RV32_control_unit rv32_control_unit_1 (
    .f7_6(RV32_Instr_Mem_data_2[30]), .f3(RV32_Instr_Mem_data_3), .Opcode(RV32_Instr_Mem_data),
    .ALU_Op(rv32_control_unit_1_alu_op), .PC_Sel(rv32_control_unit_1_pc_sel),
    .Imm_Sel(rv32_control_unit_1_imm_sel), .A_Sel(rv32_control_unit_1_a_sel),
    .B_Sel(rv32_control_unit_1_b_sel), .Mem_R(rv32_control_unit_1_mem_r), .Mem_W(rv32_control_unit_1_mem_w),
    .Reg_W(rv32_control_unit_1_reg_w), .WB_Sel(rv32_control_unit_1_wb_sel));
  Multiplexer #(.width(32)) multiplexer_2 (
    .in0(regfile_1_a_data), .in1(PC_pc_out), .out(multiplexer_2_out), .sel(rv32_control_unit_1_a_sel));
  regfile regfile_1 (
    .Data_In(multiplexer_4_out), .A_Select(rv32_instr_split_1_r1), .EN(rv32_control_unit_1_reg_w),
    .SEL(rv32_instr_split_1_rd), .Clock(clock_1_out), .B_Select(rv32_instr_split_1_r2),
    .A_data(regfile_1_a_data), .B_data(regfile_1_b_data));  // open: R
  Multiplexer #(.width(32)) multiplexer_3 (
    .in0(regfile_1_b_data), .in1(rv32_immgen_1_imm_out), .out(multiplexer_3_out),
    .sel(rv32_control_unit_1_b_sel));
  Multiplexer #(.select(2), .width(32)) multiplexer_4 (
    .in0(rv32_alu_1_alu_out), .in1(RV32_Data_Mem_dout), .in2(PC_pc_out), .out(multiplexer_4_out),
    .sel(rv32_control_unit_1_wb_sel));  // open: in3
  rv32_alu rv32_alu_1 (
    .Op_A(multiplexer_2_out), .Op_B(multiplexer_3_out), .ALU_Op_Sel(rv32_control_unit_1_alu_op),
    .ALU_Out(rv32_alu_1_alu_out));  // open: Overflow
  RAM #(.addrWidth(12), .dataWidth(32)) RV32_Data_Mem (
    .addr(rv32_alu_1_alu_out[13:2]), .we(rv32_control_unit_1_mem_w), .oe(rv32_control_unit_1_mem_r),
    .clk(clock_1_out), .din(multiplexer_3_out), .dout(RV32_Data_Mem_dout));

  // Notes on the sheet:
  //   contents of RV32_Instr_Mem (hex, n*v repeats v):
  //   f8193 3c00fef 200213
  //   32-bit  RISC-V Processor 
  //   By Jedidiah Mortey
  //   Ashesi University
endmodule

module regfile (
  input  [31:0] Data_In,
  input  R,
  input  [4:0] A_Select,
  input  EN,
  input  [4:0] SEL,
  input  Clock,
  input  [4:0] B_Select,
  output [31:0] A_data,
  output [31:0] B_data
);

  wire decoder_1_out0, decoder_1_out1, decoder_1_out2, decoder_1_out3;
  wire [3:0] decoder_1_out4, decoder_1_out8, decoder_1_out12, decoder_1_out16, decoder_1_out20,
       decoder_1_out24, decoder_1_out28;
  wire [31:0] x0, x1, x2, x3, x4, x5, x6, x7, x8, x9, x10, x11, x12, x13, x14, x15, x16, x17, x18, x19, x20,
       x21, x22, x23, x24, x25, x26, x27, x28, x29, x30, x31;

  Decoder #(.select(5)) decoder_1 (
    .out0(decoder_1_out0), .out1(decoder_1_out1), .out2(decoder_1_out2), .out3(decoder_1_out3),
    .out4(decoder_1_out4[0]), .out5(decoder_1_out4[1]), .out6(decoder_1_out4[2]), .out7(decoder_1_out4[3]),
    .out8(decoder_1_out8[0]), .out9(decoder_1_out8[1]), .out10(decoder_1_out8[2]), .out11(decoder_1_out8[3]),
    .out12(decoder_1_out12[0]), .out13(decoder_1_out12[1]), .out14(decoder_1_out12[2]),
    .out15(decoder_1_out12[3]), .out16(decoder_1_out16[0]), .out17(decoder_1_out16[1]),
    .out18(decoder_1_out16[2]), .out19(decoder_1_out16[3]), .out20(decoder_1_out20[0]),
    .out21(decoder_1_out20[1]), .out22(decoder_1_out20[2]), .out23(decoder_1_out20[3]),
    .out24(decoder_1_out24[0]), .out25(decoder_1_out24[1]), .out26(decoder_1_out24[2]),
    .out27(decoder_1_out24[3]), .out28(decoder_1_out28[0]), .out29(decoder_1_out28[1]),
    .out30(decoder_1_out28[2]), .out31(decoder_1_out28[3]), .sel(SEL), .en(EN));
  Register #(.width(32)) register_1 (.D({32{1'b0}}), .en(decoder_1_out0), .clk(Clock), .Q(x0), .clr(R));
  Register #(.width(32)) register_2 (.D(Data_In), .en(decoder_1_out1), .clk(Clock), .Q(x1), .clr(R));
  Register #(.width(32)) register_3 (.D(Data_In), .en(decoder_1_out2), .clk(Clock), .Q(x2), .clr(R));
  Register #(.width(32)) register_4 (.D(Data_In), .en(decoder_1_out3), .clk(Clock), .Q(x3), .clr(R));
  Register #(.width(32)) register_5 (.D(Data_In), .en(decoder_1_out28[1]), .clk(Clock), .Q(x5), .clr(Clock));
  Register #(.width(32)) register_6 (.D(Data_In), .en(decoder_1_out28[2]), .clk(Clock), .Q(x6), .clr(R));
  Register #(.width(32)) register_7 (.D(Data_In), .en(decoder_1_out28[3]), .clk(Clock), .Q(x7), .clr(R));
  Register #(.width(32)) register_8 (.D(Data_In), .en(decoder_1_out28[0]), .clk(Clock), .Q(x4), .clr(R));
  Register #(.width(32)) register_9 (.D(Data_In), .en(decoder_1_out24[0]), .clk(Clock), .Q(x8), .clr(R));
  Register #(.width(32)) register_10 (.D(Data_In), .en(decoder_1_out24[1]), .clk(Clock), .Q(x9), .clr(Clock));
  Register #(.width(32)) register_11 (.D(Data_In), .en(decoder_1_out24[2]), .clk(Clock), .Q(x10), .clr(R));
  Register #(.width(32)) register_12 (.D(Data_In), .en(decoder_1_out24[3]), .clk(Clock), .Q(x11), .clr(R));
  Register #(.width(32)) register_13 (.D(Data_In), .en(decoder_1_out20[0]), .clk(Clock), .Q(x12), .clr(R));
  Register #(.width(32)) register_14 (.D(Data_In), .en(decoder_1_out20[1]), .clk(Clock), .Q(x13), .clr(Clock));
  Register #(.width(32)) register_15 (.D(Data_In), .en(decoder_1_out20[2]), .clk(Clock), .Q(x14), .clr(R));
  Register #(.width(32)) register_16 (.D(Data_In), .en(decoder_1_out20[3]), .clk(Clock), .Q(x15), .clr(R));
  Register #(.width(32)) register_17 (.D(Data_In), .en(decoder_1_out16[0]), .clk(Clock), .Q(x16), .clr(R));
  Register #(.width(32)) register_18 (.D(Data_In), .en(decoder_1_out16[1]), .clk(Clock), .Q(x17), .clr(Clock));
  Register #(.width(32)) register_19 (.D(Data_In), .en(decoder_1_out16[2]), .clk(Clock), .Q(x18), .clr(R));
  Register #(.width(32)) register_20 (.D(Data_In), .en(decoder_1_out16[3]), .clk(Clock), .Q(x19), .clr(R));
  Register #(.width(32)) register_21 (.D(Data_In), .en(decoder_1_out12[0]), .clk(Clock), .Q(x20), .clr(R));
  Register #(.width(32)) register_22 (.D(Data_In), .en(decoder_1_out12[1]), .clk(Clock), .Q(x21), .clr(Clock));
  Register #(.width(32)) register_23 (.D(Data_In), .en(decoder_1_out12[2]), .clk(Clock), .Q(x22), .clr(R));
  Register #(.width(32)) register_24 (.D(Data_In), .en(decoder_1_out12[3]), .clk(Clock), .Q(x23), .clr(R));
  Register #(.width(32)) register_25 (.D(Data_In), .en(decoder_1_out8[0]), .clk(Clock), .Q(x24), .clr(R));
  Register #(.width(32)) register_26 (.D(Data_In), .en(decoder_1_out8[1]), .clk(Clock), .Q(x25), .clr(Clock));
  Register #(.width(32)) register_27 (.D(Data_In), .en(decoder_1_out8[2]), .clk(Clock), .Q(x26), .clr(R));
  Register #(.width(32)) register_28 (.D(Data_In), .en(decoder_1_out8[3]), .clk(Clock), .Q(x27), .clr(R));
  Register #(.width(32)) register_29 (.D(Data_In), .en(decoder_1_out4[0]), .clk(Clock), .Q(x28), .clr(R));
  Register #(.width(32)) register_30 (.D(Data_In), .en(decoder_1_out4[1]), .clk(Clock), .Q(x29), .clr(R));
  Register #(.width(32)) register_31 (.D(Data_In), .en(decoder_1_out4[2]), .clk(Clock), .Q(x30), .clr(R));
  Register #(.width(32)) register_32 (.D(Data_In), .en(decoder_1_out4[3]), .clk(Clock), .Q(x31), .clr(R));
  Multiplexer #(.select(5), .width(32)) multiplexer_1 (
    .in0(x0), .in1(x1), .in2(x2), .in3(x3), .in4(x4), .in5(x5), .in6(x6), .in7(x7), .in8(x8), .in9(x9),
    .in10(x10), .in11(x11), .in12(x12), .in13(x13), .in14(x14), .in15(x15), .in16(x16), .in17(x17),
    .in18(x18), .in19(x19), .in20(x20), .in21(x21), .in22(x22), .in23(x23), .in24(x24), .in25(x25),
    .in26(x26), .in27(x27), .in28(x28), .in29(x29), .in30(x30), .in31(x31), .out(A_data), .sel(A_Select));
  Multiplexer #(.select(5), .width(32)) multiplexer_2 (
    .in0(x0), .in1(x1), .in2(x2), .in3(x3), .in4(x4), .in5(x5), .in6(x6), .in7(x7), .in8(x8), .in9(x9),
    .in10(x10), .in11(x11), .in12(x12), .in13(x13), .in14(x14), .in15(x15), .in16(x16), .in17(x17),
    .in18(x18), .in19(x19), .in20(x20), .in21(x21), .in22(x22), .in23(x23), .in24(x24), .in25(x25),
    .in26(x26), .in27(x27), .in28(x28), .in29(x29), .in30(x30), .in31(x31), .out(B_data), .sel(B_Select));
endmodule

module full_adder (
  input  A,
  input  B,
  input  Ci,
  output S,
  output Co
);

  wire and_1_out, and_2_out, xor_1_out;

  xor xor_1 (xor_1_out, A, B);
  xor xor_2 (S, xor_1_out, Ci);
  and and_1 (and_1_out, xor_1_out, Ci);
  and and_2 (and_2_out, B, A);
  or or_1 (Co, and_1_out, and_2_out);
endmodule

module adder_xxxii (
  input  [31:0] Bx32,
  input  [31:0] Ax32,
  input  Sub,
  output [31:0] Ex32,
  output Overflow
);

  wire FA0_co, FA1_co, FA2_co, FA3_co, FA4_co, FA5_co, FA6_co, FA7_co, FA8_co, FA9_co, FA10_co, FA11_co,
       FA12_co, FA13_co, FA14_co, FA15_co, FA16_co, FA17_co, FA18_co, FA19_co, FA20_co, FA21_co, FA22_co,
       FA23_co, FA24_co, FA25_co, FA26_co, FA27_co, FA28_co, FA29_co, FA30_co;
  wire [31:0] multiplexer_1_out, not_1_out;

  assign not_1_out = ~Bx32;  // NOT_Gate not_1, 32 bits wide
  Multiplexer #(.width(32)) multiplexer_1 (.in0(Bx32), .in1(not_1_out), .out(multiplexer_1_out), .sel(Sub));
  full_adder FA0 (.A(Ax32[0]), .B(multiplexer_1_out[0]), .Ci(Sub), .S(Ex32[0]), .Co(FA0_co));
  full_adder FA8 (.A(Ax32[8]), .B(multiplexer_1_out[8]), .Ci(FA7_co), .S(Ex32[8]), .Co(FA8_co));
  full_adder FA16 (.A(Ax32[16]), .B(multiplexer_1_out[16]), .Ci(FA15_co), .S(Ex32[16]), .Co(FA16_co));
  full_adder FA24 (.A(Ax32[24]), .B(multiplexer_1_out[24]), .Ci(FA23_co), .S(Ex32[24]), .Co(FA24_co));
  full_adder FA2 (.A(Ax32[2]), .B(multiplexer_1_out[2]), .Ci(FA1_co), .S(Ex32[2]), .Co(FA2_co));
  full_adder FA1 (.A(Ax32[1]), .B(multiplexer_1_out[1]), .Ci(FA0_co), .S(Ex32[1]), .Co(FA1_co));
  full_adder FA10 (.A(Ax32[10]), .B(multiplexer_1_out[10]), .Ci(FA9_co), .S(Ex32[10]), .Co(FA10_co));
  full_adder FA9 (.A(Ax32[9]), .B(multiplexer_1_out[9]), .Ci(FA8_co), .S(Ex32[9]), .Co(FA9_co));
  full_adder FA18 (.A(Ax32[18]), .B(multiplexer_1_out[18]), .Ci(FA17_co), .S(Ex32[18]), .Co(FA18_co));
  full_adder FA17 (.A(Ax32[17]), .B(multiplexer_1_out[17]), .Ci(FA16_co), .S(Ex32[17]), .Co(FA17_co));
  full_adder FA26 (.A(Ax32[26]), .B(multiplexer_1_out[26]), .Ci(FA25_co), .S(Ex32[26]), .Co(FA26_co));
  full_adder FA25 (.A(Ax32[25]), .B(multiplexer_1_out[25]), .Ci(FA24_co), .S(Ex32[25]), .Co(FA25_co));
  full_adder FA3 (.A(Ax32[3]), .B(multiplexer_1_out[3]), .Ci(FA2_co), .S(Ex32[3]), .Co(FA3_co));
  full_adder FA4 (.A(Ax32[4]), .B(multiplexer_1_out[4]), .Ci(FA3_co), .S(Ex32[4]), .Co(FA4_co));
  full_adder FA11 (.A(Ax32[11]), .B(multiplexer_1_out[11]), .Ci(FA10_co), .S(Ex32[11]), .Co(FA11_co));
  full_adder FA12 (.A(Ax32[12]), .B(multiplexer_1_out[12]), .Ci(FA11_co), .S(Ex32[12]), .Co(FA12_co));
  full_adder FA19 (.A(Ax32[19]), .B(multiplexer_1_out[19]), .Ci(FA18_co), .S(Ex32[19]), .Co(FA19_co));
  full_adder FA27 (.A(Ax32[27]), .B(multiplexer_1_out[27]), .Ci(FA26_co), .S(Ex32[27]), .Co(FA27_co));
  full_adder FA5 (.A(Ax32[5]), .B(multiplexer_1_out[5]), .Ci(FA4_co), .S(Ex32[5]), .Co(FA5_co));
  full_adder FA13 (.A(Ax32[13]), .B(multiplexer_1_out[13]), .Ci(FA12_co), .S(Ex32[13]), .Co(FA13_co));
  full_adder FA20 (.A(Ax32[20]), .B(multiplexer_1_out[20]), .Ci(FA19_co), .S(Ex32[20]), .Co(FA20_co));
  full_adder FA21 (.A(Ax32[21]), .B(multiplexer_1_out[21]), .Ci(FA20_co), .S(Ex32[21]), .Co(FA21_co));
  full_adder FA28 (.A(Ax32[28]), .B(multiplexer_1_out[28]), .Ci(FA27_co), .S(Ex32[28]), .Co(FA28_co));
  full_adder FA29 (.A(Ax32[29]), .B(multiplexer_1_out[29]), .Ci(FA28_co), .S(Ex32[29]), .Co(FA29_co));
  full_adder FA6 (.A(Ax32[6]), .B(multiplexer_1_out[6]), .Ci(FA5_co), .S(Ex32[6]), .Co(FA6_co));
  full_adder FA7 (.A(Ax32[7]), .B(multiplexer_1_out[7]), .Ci(FA6_co), .S(Ex32[7]), .Co(FA7_co));
  full_adder FA14 (.A(Ax32[14]), .B(multiplexer_1_out[14]), .Ci(FA13_co), .S(Ex32[14]), .Co(FA14_co));
  full_adder FA15 (.A(Ax32[15]), .B(multiplexer_1_out[15]), .Ci(FA14_co), .S(Ex32[15]), .Co(FA15_co));
  full_adder FA22 (.A(Ax32[22]), .B(multiplexer_1_out[22]), .Ci(FA21_co), .S(Ex32[22]), .Co(FA22_co));
  full_adder FA23 (.A(Ax32[23]), .B(multiplexer_1_out[23]), .Ci(FA22_co), .S(Ex32[23]), .Co(FA23_co));
  full_adder FA30 (.A(Ax32[30]), .B(multiplexer_1_out[30]), .Ci(FA29_co), .S(Ex32[30]), .Co(FA30_co));
  full_adder FA31 (.A(Ax32[31]), .B(multiplexer_1_out[31]), .Ci(FA30_co), .S(Ex32[31]), .Co(Overflow));
endmodule

module rv32_pc (
  input  [31:0] Branch_Address,
  input  Branch,
  input  Clock,
  input  ResetPC,
  output [31:0] PC_Out
);

  wire [31:0] adder_1_out, multiplexer_1_out;

  Multiplexer #(.width(32)) multiplexer_1 (
    .in0(adder_1_out), .in1(Branch_Address), .out(multiplexer_1_out), .sel(Branch));
  Register #(.width(32)) register_1 (.D(multiplexer_1_out), .en(1'b1), .clk(Clock), .Q(PC_Out), .clr(ResetPC));
  Adder #(.width(32)) adder_1 (.a(PC_Out), .b(32'h4), .out(adder_1_out));  // open: cin, cout
endmodule

module rv32_alu (
  input  [31:0] Op_A,
  input  [31:0] Op_B,
  input  [3:0] ALU_Op_Sel,
  output Overflow,
  output [31:0] ALU_Out
);

  wire comparator_1_lt, comparator_2_lt;
  wire [31:0] ALU_ex32, bit_extender_1_out, bit_extender_2_out, multiplexer_1_out, nand_1_out, nor_1_out,
       not_1_out, not_2_out, not_3_out, shifter_1_out, shifter_2_out, shifter_3_out, xnor_1_out;

  Shifter #(.shift("lr"), .width(32)) shifter_1 (.in(Op_A), .\dist (Op_B[4:0]), .out(shifter_1_out));
  Shifter #(.shift("ar"), .width(32)) shifter_2 (.in(Op_A), .\dist (Op_B[4:0]), .out(shifter_2_out));
  Shifter #(.width(32)) shifter_3 (.in(Op_A), .\dist (Op_B[4:0]), .out(shifter_3_out));
  Comparator #(.width(32)) comparator_1 (.a(Op_A), .b(Op_B), .lt(comparator_1_lt));  // open: gt, eq
  Comparator #(.width(32)) comparator_2 (.a(Op_A), .b(Op_B), .lt(comparator_2_lt));  // open: gt, eq
  assign not_1_out = ~xnor_1_out;  // NOT_Gate not_1, 32 bits wide
  assign xnor_1_out = ~(Op_B ^ Op_A);  // XNOR_Gate xnor_1, 32 bits wide
  assign nor_1_out = ~(Op_B | Op_A);  // NOR_Gate nor_1, 32 bits wide
  assign not_2_out = ~nor_1_out;  // NOT_Gate not_2, 32 bits wide
  assign nand_1_out = ~(Op_B & Op_A);  // NAND_Gate nand_1, 32 bits wide
  assign not_3_out = ~nand_1_out;  // NOT_Gate not_3, 32 bits wide
  Multiplexer #(.width(32)) multiplexer_1 (
    .in0(shifter_1_out), .in1(shifter_2_out), .out(multiplexer_1_out), .sel(ALU_Op_Sel[0]));
  adder_xxxii ALU (.Ax32(Op_A), .Bx32(Op_B), .Sub(ALU_Op_Sel[0]), .Overflow(Overflow), .Ex32(ALU_ex32));
  assign bit_extender_1_out = {{31{comparator_1_lt}}, comparator_1_lt};  // Bit_Extender bit_extender_1
  assign bit_extender_2_out = {{31{comparator_2_lt}}, comparator_2_lt};  // Bit_Extender bit_extender_2
  Multiplexer #(.select(3), .width(32)) multiplexer_2 (
    .in0(ALU_ex32), .in1(shifter_3_out), .in2(bit_extender_1_out), .in3(bit_extender_2_out), .in4(not_1_out),
    .in5(multiplexer_1_out), .in6(not_2_out), .in7(not_3_out), .out(ALU_Out), .sel(ALU_Op_Sel[3:1]));

  // Other names for the same wires on the sheet: Opt = ALU_Op_Sel[0]
endmodule

module RV32_instr_split (
  input  [31:0] Instr32,
  output [6:0] opcode,
  output [4:0] rd,
  output [2:0] funct3,
  output [4:0] r2,
  output [4:0] r1,
  output [6:0] funct7,
  output [24:0] to_Imm
);


  assign funct3 = Instr32[14:12];
  assign funct7 = Instr32[31:25];
  assign opcode = Instr32[6:0];
  assign r1 = Instr32[24:20];
  assign r2 = Instr32[19:15];
  assign rd = Instr32[11:7];
  assign to_Imm = Instr32[31:7];
endmodule

// type_decode
module rv32_typedecode (
  input  [6:0] Opcode,
  output R_Type,
  output I_Type,
  output I_Load,
  output S_Type,
  output SB_Type,
  output U_Type,
  output JAL,
  output LUI,
  output JALR
);

  wire and_1_out, and_3_out;
  wire [6:0] xnor_1_out, xnor_2_out, xnor_3_out, xnor_4_out, xnor_5_out, xnor_6_out, xnor_7_out, xnor_8_out,
       xnor_9_out, xnor_10_out;

  assign xnor_1_out = ~(Opcode ^ 7'b0111011);  // XNOR_Gate xnor_1, 7 bits wide
  assign xnor_2_out = ~(Opcode ^ 7'b0010011);  // XNOR_Gate xnor_2, 7 bits wide
  and and_1 (and_1_out, xnor_3_out[0], xnor_3_out[1], xnor_3_out[2], xnor_3_out[3], xnor_3_out[4], xnor_3_out[5], xnor_3_out[6]);
  assign xnor_3_out = ~(Opcode ^ 7'b0110011);  // XNOR_Gate xnor_3, 7 bits wide
  and and_2 (I_Type, xnor_2_out[0], xnor_2_out[1], xnor_2_out[2], xnor_2_out[3], xnor_2_out[4], xnor_2_out[5], xnor_2_out[6]);
  assign xnor_4_out = ~(Opcode ^ 7'b0000011);  // XNOR_Gate xnor_4, 7 bits wide
  assign xnor_5_out = ~(Opcode ^ 7'b0100011);  // XNOR_Gate xnor_5, 7 bits wide
  assign xnor_6_out = ~(Opcode ^ 7'b1100011);  // XNOR_Gate xnor_6, 7 bits wide
  assign xnor_7_out = ~(Opcode ^ 7'b0010111);  // XNOR_Gate xnor_7, 7 bits wide
  assign xnor_8_out = ~(Opcode ^ 7'b1101111);  // XNOR_Gate xnor_8, 7 bits wide
  assign xnor_9_out = ~(Opcode ^ 7'b0110111);  // XNOR_Gate xnor_9, 7 bits wide
  assign xnor_10_out = ~(Opcode ^ 7'b1100111);  // XNOR_Gate xnor_10, 7 bits wide
  and and_3 (and_3_out, xnor_1_out[0], xnor_1_out[1], xnor_1_out[2], xnor_1_out[3], xnor_1_out[4], xnor_1_out[5], xnor_1_out[6]);
  and and_4 (I_Load, xnor_4_out[0], xnor_4_out[1], xnor_4_out[2], xnor_4_out[3], xnor_4_out[4], xnor_4_out[5], xnor_4_out[6]);
  and and_5 (S_Type, xnor_5_out[0], xnor_5_out[1], xnor_5_out[2], xnor_5_out[3], xnor_5_out[4], xnor_5_out[5], xnor_5_out[6]);
  and and_6 (SB_Type, xnor_6_out[0], xnor_6_out[1], xnor_6_out[2], xnor_6_out[3], xnor_6_out[4], xnor_6_out[5], xnor_6_out[6]);
  and and_7 (U_Type, xnor_7_out[0], xnor_7_out[1], xnor_7_out[2], xnor_7_out[3], xnor_7_out[4], xnor_7_out[5], xnor_7_out[6]);
  and and_8 (LUI, xnor_9_out[0], xnor_9_out[1], xnor_9_out[2], xnor_9_out[3], xnor_9_out[4], xnor_9_out[5], xnor_9_out[6]);
  and and_9 (JALR, xnor_10_out[0], xnor_10_out[1], xnor_10_out[2], xnor_10_out[3], xnor_10_out[4], xnor_10_out[5], xnor_10_out[6]);
  or or_1 (R_Type, and_1_out, and_3_out);
  and and_10 (JAL, xnor_8_out[0], xnor_8_out[1], xnor_8_out[2], xnor_8_out[3], xnor_8_out[4], xnor_8_out[5], xnor_8_out[6]);
endmodule

module RV32_ImmGen (
  input  [31:0] Instr,
  input  [2:0] Imm_Sel,
  output [31:0] Imm_Out
);

  wire [31:0] bit_extender_1_out, bit_extender_2_out, bit_extender_3_out, bit_extender_4_out;

  assign bit_extender_1_out = {{20{Instr[31]}}, {Instr[31], Instr[7], Instr[30:25], Instr[11:8]}};  // Bit_Extender bit_extender_1
  assign bit_extender_2_out = {{20{Instr[31]}}, {Instr[31:25], Instr[11:7]}};  // Bit_Extender bit_extender_2
  assign bit_extender_3_out = {{12{Instr[31]}}, Instr[31:12]};  // Bit_Extender bit_extender_3
  assign bit_extender_4_out = {{20{Instr[31]}}, Instr[31:20]};  // Bit_Extender bit_extender_4
  Multiplexer #(.select(3), .width(32)) multiplexer_1 (
    .in0(bit_extender_4_out), .in1(bit_extender_2_out), .in2(bit_extender_1_out), .in3(bit_extender_3_out),
    .in4({{12{1'b0}}, Instr[31], Instr[19:12], Instr[20], Instr[30:21]}), .out(Imm_Out), .sel(Imm_Sel));  // open: in5, in6, in7

  // Notes on the sheet:
  //   Imm. SB
  //   Imm. U
  //   Imm. S
  //   Imm. J
  //   Imm. I
endmodule

module RV32_control_unit (
  input  f7_6,
  input  [2:0] f3,
  input  [6:0] Opcode,
  output [3:0] ALU_Op,
  output PC_Sel,
  output [2:0] Imm_Sel,
  output A_Sel,
  output B_Sel,
  output Mem_R,
  output Mem_W,
  output Reg_W,
  output [1:0] WB_Sel
);

  wire comparator_1_eq, comparator_2_eq, or_1_out;

  ROM #(.addrWidth(5), .dataWidth(11)) Ctrl_Mem (
    .addr(Opcode[6:2]), .data({WB_Sel, Reg_W, Mem_W, Mem_R, B_Sel, A_Sel, Imm_Sel, PC_Sel}));
  Comparator #(.width(5)) comparator_1 (.a(5'b01100), .b(Opcode[6:2]), .eq(comparator_1_eq));  // open: gt, lt
  Comparator #(.width(5)) comparator_2 (.a(5'b01100), .b(Opcode[6:2]), .eq(comparator_2_eq));  // open: gt, lt
  or or_1 (or_1_out, comparator_1_eq, comparator_2_eq);
  Multiplexer #(.width(4)) multiplexer_1 (.in0({f3, f7_6}), .in1(4'b0000), .out(ALU_Op), .sel(or_1_out));

  // Notes on the sheet:
  //   contents of Ctrl_Mem (hex, n*v repeats v):
  //   35 0 0 0 34 274 0 0 a8 0 0 0 14 1f6 14 9*0 570 436
endmodule

module RV32_ALU_Op_Sel (
  input  [3:0] Type_to4,
  input  [2:0] F3,
  input  F7
);

  ROM #(.addrWidth(4), .dataWidth(12)) Ctrl_Signals (.addr(Type_to4));  // open: data

  // Notes on the sheet:
  //   contents of Ctrl_Signals (hex, n*v repeats v):
  //   40c 410 41c 45d 114 158 478 44d 20f
endmodule
